# Fritzing sketch ADXL345_circuit (saved by Fritzing 0.9.3b)

parts:
  元件1 = Triple Axis Accelerometer Breakout - ADXL345
  U1 = ESP32S-HiLetgo [part_number=ESP32S-HiLetgo]

nets:
  GND: 元件1.GND, U1.GND
  VCC: 元件1.VCC, U1.VIN
  N1: 元件1.CS, U1.GPIO5
  N2: 元件1.SDO, U1.GPIO19
  N3: 元件1.SDA, U1.GPIO13
  N4: 元件1.SCL, U1.GPIO18

custom parts:
  ESP32S-HiLetgo: HiLetgo ESP-WROOM-32 ESP32 ESP-32S Development Board 2.4GHz Dual-Mode WiFi + Bluetooth Dual Cores Microcontroller The ESP32 integrated with Antenna switches, RF Balun, power amplifiers, low-noise amplifiers, filters, and management modules, and the entire solution occupies the least area of PCB. 2.4 GHz Wi-Fi plus Bluetooth dual-mode chip, with TSMC Ultra-low power consumption 40nm technology,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
