# Fritzing sketch Amg8xx_circuit (saved by Fritzing 0.9.3b)

parts:
  U1 = ESP32S-HiLetgo [part_number=ESP32S-HiLetgo]
  Composant1 = Adafruit AMG8833 [part_number="Adafruit #3538"]
  LED1 = smd LED [color="Red (633nm)" package="0603 [SMD]"]
  R1 = Resistor [tolerance=±5% resistance=220 package="0603 [SMD]"]

nets:
  N1: U1.3.3, Composant1.3.3V
  GND: U1.GND, Composant1.GND, LED1.cathode
  N2: U1.GPIO0, R1.Pin_1
  N3: U1.GPIO17, Composant1.INT
  N4: U1.GPIO21, Composant1.SDA
  N5: U1.GPIO22, Composant1.SCL

custom parts:
  ESP32S-HiLetgo: HiLetgo ESP-WROOM-32 ESP32 ESP-32S Development Board 2.4GHz Dual-Mode WiFi + Bluetooth Dual Cores Microcontroller The ESP32 integrated with Antenna switches, RF Balun, power amplifiers, low-noise amplifiers, filters, and management modules, and the entire solution occupies the least area of PCB. 2.4 GHz Wi-Fi plus Bluetooth dual-mode chip, with TSMC Ultra-low power consumption 40nm technology,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
  Adafruit AMG8833: Add heat-vision to your project and with an Adafruit AMG8833 Grid-EYE Breakout! This sensor from Panasonic is an 8x8 array of IR thermal sensors. When connected to your microcontroller (or raspberry Pi) it will return an array of 64 individual infrared temperature readings over I2C. It's like those fancy thermal cameras, but compact and simple enough for easy integration. This part will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
