# Fritzing sketch BH1750FVI_Circuit (saved by Fritzing 0.9.3b)

parts:
  Часть2 = BH1750
  U1 = ESP32S-HiLetgo [part_number=ESP32S-HiLetgo]

nets:
  N1: Часть2.VCC, U1.3.3
  GND: Часть2.GND, Часть2.ADDR, U1.GND
  N2: Часть2.SCL, U1.GPIO22
  N3: Часть2.SDA, U1.GPIO21

custom parts:
  BH1750: Light Sensor
  ESP32S-HiLetgo: HiLetgo ESP-WROOM-32 ESP32 ESP-32S Development Board 2.4GHz Dual-Mode WiFi + Bluetooth Dual Cores Microcontroller The ESP32 integrated with Antenna switches, RF Balun, power amplifiers, low-noise amplifiers, filters, and management modules, and the entire solution occupies the least area of PCB. 2.4 GHz Wi-Fi plus Bluetooth dual-mode chip, with TSMC Ultra-low power consumption 40nm technology,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
