# Fritzing sketch ccs811 (saved by Fritzing 0.9.3b)

parts:
  Composant1 = Adafruit CCS811
  U1 = ESP32S-HiLetgo [part_number=ESP32S-HiLetgo]

nets:
  VIN: Composant1.VIN, Composant1.GND, U1.VIN, U1.GND
  N1: Composant1.SDA, U1.GPIO21
  N2: Composant1.SCL, U1.GPIO22
  N3: Composant1.!WAKE, U1.GPIO17
  N4: Composant1.!INT, U1.GPIO16

custom parts:
  ESP32S-HiLetgo: HiLetgo ESP-WROOM-32 ESP32 ESP-32S Development Board 2.4GHz Dual-Mode WiFi + Bluetooth Dual Cores Microcontroller The ESP32 integrated with Antenna switches, RF Balun, power amplifiers, low-noise amplifiers, filters, and management modules, and the entire solution occupies the least area of PCB. 2.4 GHz Wi-Fi plus Bluetooth dual-mode chip, with TSMC Ultra-low power consumption 40nm technology,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
