# Fritzing sketch DCMotor2pinWithBiDirectionalPin (saved by Fritzing 0.9.3b)

parts:
  Part1 = MD13S
  M1 = DC Motor
  U1 = ESP32S-HiLetgo [part_number=ESP32S-HiLetgo]

nets:
  N1: Part1.no_name_yet#connector_DIR1, U1.GPIO27
  N2: Part1.no_name_yet#connector_G0, U1.GND
  N3: Part1.no_name_yet#connector_MA1, M1.pin_2
  N4: Part1.no_name_yet#connector_MB1, M1.pin_1
  N5: Part1.no_name_yet#connector_PWM1, U1.GPIO14

custom parts:
  ESP32S-HiLetgo: HiLetgo ESP-WROOM-32 ESP32 ESP-32S Development Board 2.4GHz Dual-Mode WiFi + Bluetooth Dual Cores Microcontroller The ESP32 integrated with Antenna switches, RF Balun, power amplifiers, low-noise amplifiers, filters, and management modules, and the entire solution occupies the least area of PCB. 2.4 GHz Wi-Fi plus Bluetooth dual-mode chip, with TSMC Ultra-low power consumption 40nm technology,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
