# Fritzing sketch dcmotor (saved by Fritzing 0.9.3b)
breadboards: 1

parts:
  S1 = H-Bridge with L298N
  M1 = DC Motor
  M2 = DC Motor
  VCC1 = Battery block 9V
  U1 = ESP32S-HiLetgo [part_number=ESP32S-HiLetgo]

nets:
  N1: S1.12V, VCC1.+
  GND: S1.GND, VCC1.-, U1.GND
  N2: S1.5V, U1.3.3
  N3: S1.ENA, U1.GPIO27
  N4: S1.IN1, U1.GPIO25
  N5: S1.IN2, U1.GPIO32
  N6: S1.IN3, U1.GPIO34
  N7: S1.IN4, U1.GPIO36
  N8: S1.ENB, S1.ENB-5V
  N9: S1.M1-01, M2.pin_2
  N10: S1.M1-02, M2.pin_1
  N11: S1.M2-01, M1.pin_2
  N12: S1.M2-02, M1.pin_1

notes:
  2 pin setup
  3 pin setup

custom parts:
  H-Bridge with L298N: h-bridge
  ESP32S-HiLetgo: HiLetgo ESP-WROOM-32 ESP32 ESP-32S Development Board 2.4GHz Dual-Mode WiFi + Bluetooth Dual Cores Microcontroller The ESP32 integrated with Antenna switches, RF Balun, power amplifiers, low-noise amplifiers, filters, and management modules, and the entire solution occupies the least area of PCB. 2.4 GHz Wi-Fi plus Bluetooth dual-mode chip, with TSMC Ultra-low power consumption 40nm technology,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
