# Fritzing sketch DHT12_circuit (saved by Fritzing 0.9.3b)
breadboards: 1

parts:
  DHT3 = DHT11 Humitidy and Temperature Sensor
  R1 = Resistor [tolerance=±5% resistance=4.7k package=THT]
  R2 = Resistor [tolerance=±5% resistance=4.7k package=THT]
  U1 = ESP32S-HiLetgo [part_number=ESP32S-HiLetgo]

nets:
  N1: DHT3.VDD, R1.Pin_1, R2.Pin_1, U1.3.3
  N2: DHT3.DATA, R1.Pin_0, U1.GPIO21, U1.GPIO3
  N3: DHT3.NULL, U1.GND
  N4: DHT3.GND, R2.Pin_0, U1.GPIO22

notes:
  DHT12

custom parts:
  DHT11 Humitidy and Temperature Sensor: DHT11 Humidity and Temperature Sensor
  ESP32S-HiLetgo: HiLetgo ESP-WROOM-32 ESP32 ESP-32S Development Board 2.4GHz Dual-Mode WiFi + Bluetooth Dual Cores Microcontroller The ESP32 integrated with Antenna switches, RF Balun, power amplifiers, low-noise amplifiers, filters, and management modules, and the entire solution occupies the least area of PCB. 2.4 GHz Wi-Fi plus Bluetooth dual-mode chip, with TSMC Ultra-low power consumption 40nm technology,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
