# Fritzing sketch Ds1302 (saved by Fritzing 0.9.3b)

parts:
  M1 = DOIT Esp32 DevKit v1 (30 pins long, 11 pins width) [part_number=ESP32S-PIN30]
  PCB2 = RTC_DS1302_module

nets:
  3V3: M1.3V3, PCB2.VCC
  GND: M1.GND, PCB2.GND
  N1: M1.D14, PCB2.RST
  N2: M1.D12, PCB2.DAT
  N3: M1.D13, PCB2.CLK

custom parts:
  DOIT Esp32 DevKit v1 (30 pins long, 11 pins width): The DOIT Esp32 DevKit v1 is one of the development board created by DOIT to evaluate the ESP-WROOM-32 module. It is based on the ESP32 microcontroller that boasts Wifi, Bluetooth, Ethernet and Low Power support all in a single chip. (vanepp) made breadboard work, adjusted pin numbering and labels and reduced size of schematic and cleaned up pcb. This chip is 30pins long (2 x15) and 11 pins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
  RTC_DS1302_module: Arduino module DS1302 SPI Real Time Clock
