# Fritzing sketch HMC5883L_circuit (saved by Fritzing 0.9.3b)

parts:
  Componente2 = Triple Axis Magnetometer - HMC5883 Breakout
  U1 = ESP32S-HiLetgo [part_number=ESP32S-HiLetgo]

nets:
  GND: Componente2.GND, U1.GND
  N1: Componente2.VCC, U1.3.3
  N2: Componente2.SDA, U1.GPIO21
  N3: Componente2.SCL, U1.GPIO22

custom parts:
  ESP32S-HiLetgo: HiLetgo ESP-WROOM-32 ESP32 ESP-32S Development Board 2.4GHz Dual-Mode WiFi + Bluetooth Dual Cores Microcontroller The ESP32 integrated with Antenna switches, RF Balun, power amplifiers, low-noise amplifiers, filters, and management modules, and the entire solution occupies the least area of PCB. 2.4 GHz Wi-Fi plus Bluetooth dual-mode chip, with TSMC Ultra-low power consumption 40nm technology,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
