# Fritzing sketch 4x4kb_via_mcp23017 (saved by Fritzing 0.9.3b)

parts:
  S1 = Pushbutton [package="[THT]"]
  S2 = Pushbutton [package="[THT]"]
  S3 = Pushbutton [package="[THT]"]
  S4 = Pushbutton [package="[THT]"]
  S5 = Pushbutton [package="[THT]"]
  S6 = Pushbutton [package="[THT]"]
  S7 = Pushbutton [package="[THT]"]
  S8 = Pushbutton [package="[THT]"]
  S9 = Pushbutton [package="[THT]"]
  S10 = Pushbutton [package="[THT]"]
  S11 = Pushbutton [package="[THT]"]
  S12 = Pushbutton [package="[THT]"]
  S13 = Pushbutton [package="[THT]"]
  S14 = Pushbutton [package="[THT]"]
  S15 = Pushbutton [package="[THT]"]
  S16 = Pushbutton [package="[THT]"]
  R1 = Resistor [tolerance=±5% resistance=22k package=THT]
  R2 = Resistor [tolerance=±5% resistance=22k package=THT]
  R3 = Resistor [tolerance=±5% resistance=22k package=THT]
  R4 = Resistor [tolerance=±5% resistance=22k package=THT]
  U1 = mystery part, 28 pins [chip_label=MCP23017]
  U2 = ESP32S-HiLetgo [part_number=ESP32S-HiLetgo]

nets:
  N1: S1.Pin_1, S1.Pin_2, S2.Pin_1, S2.Pin_2, S3.Pin_1, S3.Pin_2, S4.Pin_1, S4.Pin_2, R4.Pin_1, U1.pin25
  N2: S1.Pin_3, S7.Pin_3, S10.Pin_3, S16.Pin_3, U1.pin1
  N3: S2.Pin_3, S8.Pin_3, S12.Pin_3, S14.Pin_3, U1.pin2
  N4: S3.Pin_3, S6.Pin_3, S9.Pin_3, S13.Pin_3, U1.pin3
  N5: S4.Pin_3, S5.Pin_3, S11.Pin_3, S15.Pin_3, U1.pin4
  N6: S5.Pin_1, S5.Pin_2, S6.Pin_1, S6.Pin_2, S7.Pin_1, S7.Pin_2, S8.Pin_1, S8.Pin_2, R3.Pin_1, U1.pin26
  N7: S9.Pin_1, S9.Pin_2, S10.Pin_1, S10.Pin_2, S11.Pin_1, S11.Pin_2, S12.Pin_1, S12.Pin_2, R2.Pin_1, U1.pin27
  N8: S13.Pin_1, S13.Pin_2, S14.Pin_1, S14.Pin_2, S15.Pin_1, S15.Pin_2, S16.Pin_1, S16.Pin_2, R1.Pin_1, U1.pin28
  N9: R1.Pin_0, R2.Pin_0, R3.Pin_0, R4.Pin_0, U1.pin10, U1.pin15, U1.pin16, U1.pin17, U2.GND
  N10: U1.pin9, U1.pin18, U2.3.3
  N11: U1.pin12, U2.GPIO22
  N12: U1.pin13, U2.GPIO21

custom parts:
  ESP32S-HiLetgo: HiLetgo ESP-WROOM-32 ESP32 ESP-32S Development Board 2.4GHz Dual-Mode WiFi + Bluetooth Dual Cores Microcontroller The ESP32 integrated with Antenna switches, RF Balun, power amplifiers, low-noise amplifiers, filters, and management modules, and the entire solution occupies the least area of PCB. 2.4 GHz Wi-Fi plus Bluetooth dual-mode chip, with TSMC Ultra-low power consumption 40nm technology,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
