# Fritzing sketch rpi-llc200d3sh (saved by Fritzing 0.9.3b)
breadboards: 1

parts:
  M1 = LLC200D3SH [package=THT]
  U1 = ESP32S-HiLetgo [part_number=ESP32S-HiLetgo]

nets:
  N1: M1.pin1, U1.3.3
  N2: M1.pin2, U1.GPIO16
  N3: M1.pin3, U1.GND

custom parts:
  LLC200D3SH: Optomax Digital liquid level switch..
  ESP32S-HiLetgo: HiLetgo ESP-WROOM-32 ESP32 ESP-32S Development Board 2.4GHz Dual-Mode WiFi + Bluetooth Dual Cores Microcontroller The ESP32 integrated with Antenna switches, RF Balun, power amplifiers, low-noise amplifiers, filters, and management modules, and the entire solution occupies the least area of PCB. 2.4 GHz Wi-Fi plus Bluetooth dual-mode chip, with TSMC Ultra-low power consumption 40nm technology,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
