# Fritzing sketch MAX31856_circuit (saved by Fritzing 0.9.3b)

parts:
  U1 = ESP32S-HiLetgo [part_number=ESP32S-HiLetgo]
  Composant1 = Adafruit MAX31856 Thermocouple Amp [part_number="Adafruit #3263"]

nets:
  N1: U1.3.3, Composant1.VIN
  N2: U1.GPIO12, Composant1.SDI
  N3: U1.GPIO5, Composant1.!CS
  N4: U1.GPIO18, Composant1.SCK
  N5: U1.GPIO19, Composant1.SDO
  GND: U1.GND, Composant1.GND

custom parts:
  ESP32S-HiLetgo: HiLetgo ESP-WROOM-32 ESP32 ESP-32S Development Board 2.4GHz Dual-Mode WiFi + Bluetooth Dual Cores Microcontroller The ESP32 integrated with Antenna switches, RF Balun, power amplifiers, low-noise amplifiers, filters, and management modules, and the entire solution occupies the least area of PCB. 2.4 GHz Wi-Fi plus Bluetooth dual-mode chip, with TSMC Ultra-low power consumption 40nm technology,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
  Adafruit MAX31856 Thermocouple Amp: Thermocouples are very sensitive, requiring a good amplifier with a cold-compensation reference, as well as calculations to handle any non-linearities. For a long time we've suggested our MAX31855K breakout, which works great but is only for K-type thermocouples. Now we're happy to offer a great new thermocouple amplifier/converter that can handle just about any type of thermocouple, and even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
