# Fritzing sketch MAX31865_circuit (saved by Fritzing 0.9.3b)

parts:
  Part1 = Adafruit MAX31865 RTD Sensor Breakout [part_number="Adafruit #3328"]
  U1 = ESP32S-HiLetgo [part_number=ESP32S-HiLetgo]

nets:
  N1: Part1.VIN, U1.3.3
  GND: Part1.GND, U1.GND
  N2: Part1.SCLK, U1.GPIO18
  N3: Part1.SDO, U1.GPIO19
  N4: Part1.SDI, U1.GPIO13
  N5: Part1.CS, U1.GPIO5

custom parts:
  Adafruit MAX31865 RTD Sensor Breakout: For precision temperature sensing, nothing beats a Platinum RTD. Resistance temperature detectors (RTDs) are temperature sensors that contain a resistor that changes resistance value as its temperature changes, basically a kind of thermistor. In this sensor, the resistor is actually a small strip of Platinum with a resistance of 100 ohms at 0°C, thus the name PT100. Compared to most NTC/PTC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
  ESP32S-HiLetgo: HiLetgo ESP-WROOM-32 ESP32 ESP-32S Development Board 2.4GHz Dual-Mode WiFi + Bluetooth Dual Cores Microcontroller The ESP32 integrated with Antenna switches, RF Balun, power amplifiers, low-noise amplifiers, filters, and management modules, and the entire solution occupies the least area of PCB. 2.4 GHz Wi-Fi plus Bluetooth dual-mode chip, with TSMC Ultra-low power consumption 40nm technology,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
