# Fritzing sketch Schema (saved by Fritzing 0.9.3b)

parts:
  8x8_LED_matrix_MAX1 = 8x8 Red 8x8 LED Matrix with MAX7219
  8x8_LED_matrix_MAX2 = 8x8 Red 8x8 LED Matrix with MAX7219
  U1 = ESP32S-HiLetgo [part_number=ESP32S-HiLetgo]

nets:
  VCC: 8x8_LED_matrix_MAX1.VCC, 8x8_LED_matrix_MAX1.VCC_PT, 8x8_LED_matrix_MAX2.VCC, 8x8_LED_matrix_MAX2.VCC_PT, U1.VIN
  GND: 8x8_LED_matrix_MAX1.GND, 8x8_LED_matrix_MAX1.CLK_PT, 8x8_LED_matrix_MAX2.GND_PT, 8x8_LED_matrix_MAX2.CLK, U1.GND
  N1: 8x8_LED_matrix_MAX1.GND_PT, 8x8_LED_matrix_MAX1.CLK, 8x8_LED_matrix_MAX2.GND, 8x8_LED_matrix_MAX2.CLK_PT, U1.GPIO18
  N2: 8x8_LED_matrix_MAX1.DIN, U1.GPIO13
  N3: 8x8_LED_matrix_MAX1.DIN_CHN, 8x8_LED_matrix_MAX1.CS, 8x8_LED_matrix_MAX2.DIN, U1.GPIO5
  N4: 8x8_LED_matrix_MAX1.CS_PT, 8x8_LED_matrix_MAX2.DIN_CHN, 8x8_LED_matrix_MAX2.CS

custom parts:
  8x8 Red 8x8 LED Matrix with MAX7219: Description: 8 by 8 red LED matrix with a MAX7219 controller.
  ESP32S-HiLetgo: HiLetgo ESP-WROOM-32 ESP32 ESP-32S Development Board 2.4GHz Dual-Mode WiFi + Bluetooth Dual Cores Microcontroller The ESP32 integrated with Antenna switches, RF Balun, power amplifiers, low-noise amplifiers, filters, and management modules, and the entire solution occupies the least area of PCB. 2.4 GHz Wi-Fi plus Bluetooth dual-mode chip, with TSMC Ultra-low power consumption 40nm technology,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
