# Fritzing sketch rpi_led_adc_i2c (saved by Fritzing 0.9.3b)
breadboards: 1

parts:
  ADC2 = MCP3428 [package=dil14]  # not connected
  LED1 = LED - 5mm [color="Red (633nm)" package="5 mm [THT]"]
  R1 = Resistor [tolerance=±5% resistance=220 package=THT]
  U1 = ESP32S-HiLetgo [part_number=ESP32S-HiLetgo]

nets:
  N1: LED1.cathode, U1.GND
  N2: LED1.anode, R1.Pin_0
  N3: R1.Pin_1, U1.3.3

custom parts:
  MCP3428: 2.7V 4-Channel 16-Bit A/D Converters with I2C Interface from Microchip
  ESP32S-HiLetgo: HiLetgo ESP-WROOM-32 ESP32 ESP-32S Development Board 2.4GHz Dual-Mode WiFi + Bluetooth Dual Cores Microcontroller The ESP32 integrated with Antenna switches, RF Balun, power amplifiers, low-noise amplifiers, filters, and management modules, and the entire solution occupies the least area of PCB. 2.4 GHz Wi-Fi plus Bluetooth dual-mode chip, with TSMC Ultra-low power consumption 40nm technology,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
