# Fritzing sketch rpi-trimpot_gpio (saved by Fritzing 0.9.3b)
breadboards: 1

parts:
  POT1 = Breadboard Trimpot
  IC1 = MCP3008 8-channel 10-bit ADC [part_number=MCP3008]
  U1 = ESP32S-HiLetgo [part_number=ESP32S-HiLetgo]

nets:
  N1: POT1.PIN1, IC1.no_name_yet#9, IC1.no_name_yet#14, U1.GND
  N2: POT1.PIN2, IC1.no_name_yet#1
  N3: POT1.PIN3, IC1.no_name_yet#15, IC1.no_name_yet#16, U1.3.3
  N4: IC1.no_name_yet#10, U1.GPIO5
  N5: IC1.no_name_yet#11, U1.GPIO19
  N6: IC1.no_name_yet#12, U1.GPIO21
  N7: IC1.no_name_yet#13, U1.GPIO22

custom parts:
  ESP32S-HiLetgo: HiLetgo ESP-WROOM-32 ESP32 ESP-32S Development Board 2.4GHz Dual-Mode WiFi + Bluetooth Dual Cores Microcontroller The ESP32 integrated with Antenna switches, RF Balun, power amplifiers, low-noise amplifiers, filters, and management modules, and the entire solution occupies the least area of PCB. 2.4 GHz Wi-Fi plus Bluetooth dual-mode chip, with TSMC Ultra-low power consumption 40nm technology,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
