# Fritzing sketch Mhz19B (saved by Fritzing 0.9.9b)

parts:
  TD-er1 = MH-Z19 CO2 sensor [part_number=MH-Z19]
  U1 = ESP32S-HiLetgo [part_number=ESP32S-HiLetgo]

nets:
  N1: TD-er1.RX, U1.GPIO35
  N2: TD-er1.TX, U1.GPIO32
  VIN: TD-er1.Vin, U1.VIN
  N3: TD-er1.GND, U1.GPIO11

custom parts:
  ESP32S-HiLetgo: HiLetgo ESP-WROOM-32 ESP32 ESP-32S Development Board 2.4GHz Dual-Mode WiFi + Bluetooth Dual Cores Microcontroller The ESP32 integrated with Antenna switches, RF Balun, power amplifiers, low-noise amplifiers, filters, and management modules, and the entire solution occupies the least area of PCB. 2.4 GHz Wi-Fi plus Bluetooth dual-mode chip, with TSMC Ultra-low power consumption 40nm technology,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
