# Fritzing sketch MLX90614_circuit (saved by Fritzing 0.9.3b)

parts:
  U2 = MLX90614 [package=to-39]
  U3 = ESP32S-HiLetgo [part_number=ESP32S-HiLetgo]

nets:
  N1: U2.SCL_VZ, U3.GPIO22
  N2: U2.PWM_SDA, U3.GPIO21
  N3: U2.VDD, U3.3.3
  VSS: U2.VSS, U3.GND

custom parts:
  ESP32S-HiLetgo: HiLetgo ESP-WROOM-32 ESP32 ESP-32S Development Board 2.4GHz Dual-Mode WiFi + Bluetooth Dual Cores Microcontroller The ESP32 integrated with Antenna switches, RF Balun, power amplifiers, low-noise amplifiers, filters, and management modules, and the entire solution occupies the least area of PCB. 2.4 GHz Wi-Fi plus Bluetooth dual-mode chip, with TSMC Ultra-low power consumption 40nm technology,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
