# Fritzing sketch Mpu9250 (saved by Fritzing 0.9.3b)

parts:
  MPU9250_MPU-1 = SparkFun IMU Breakout - MPU-9250 [part_number=" SEN-13762"]
  U1 = ESP32S-HiLetgo [part_number=ESP32S-HiLetgo]

nets:
  N1: MPU9250_MPU-1.SCL/SCLK, U1.GPIO22
  N2: MPU9250_MPU-1.SDA/SDI, U1.GPIO21
  N3: MPU9250_MPU-1.VDD, MPU9250_MPU-1.VDDIO, U1.3.3
  GND: MPU9250_MPU-1.GND, MPU9250_MPU-1.FSYNC, MPU9250_MPU-1.AD0/SDO, U1.GND

custom parts:
  ESP32S-HiLetgo: HiLetgo ESP-WROOM-32 ESP32 ESP-32S Development Board 2.4GHz Dual-Mode WiFi + Bluetooth Dual Cores Microcontroller The ESP32 integrated with Antenna switches, RF Balun, power amplifiers, low-noise amplifiers, filters, and management modules, and the entire solution occupies the least area of PCB. 2.4 GHz Wi-Fi plus Bluetooth dual-mode chip, with TSMC Ultra-low power consumption 40nm technology,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
