# Fritzing sketch Pca95x4_I2c_WriteLeds (saved by Fritzing 0.9.3b)
breadboards: 1

parts:
  R1 = Resistor [tolerance=±5% resistance=470 package=THT]
  LED1 = LED - 5mm [color="Red (633nm)" package="5 mm [THT]"]
  R2 = Resistor [tolerance=±5% resistance=10k package=THT]
  R3 = Resistor [tolerance=±5% resistance=470 package=THT]
  LED2 = LED - 5mm [color="Red (633nm)" package="5 mm [THT]"]
  R4 = Resistor [tolerance=±5% resistance=470 package=THT]
  LED3 = LED - 5mm [color="Red (633nm)" package="5 mm [THT]"]
  R5 = Resistor [tolerance=±5% resistance=470 package=THT]
  LED4 = LED - 5mm [color="Red (633nm)" package="5 mm [THT]"]
  R6 = Resistor [tolerance=±5% resistance=470 package=THT]
  LED5 = LED - 5mm [color="Red (633nm)" package="5 mm [THT]"]
  LED6 = LED - 5mm [color="Red (633nm)" package="5 mm [THT]"]
  LED7 = LED - 5mm [color="Red (633nm)" package="5 mm [THT]"]
  LED8 = LED - 5mm [color="Red (633nm)" package="5 mm [THT]"]
  R7 = Resistor [tolerance=±5% resistance=470 package=THT]
  R8 = Resistor [tolerance=±5% resistance=470 package=THT]
  R9 = Resistor [tolerance=±5% resistance=470 package=THT]
  IOE1 = Pca95x4 [package=dil16]
  U1 = ESP32S-HiLetgo [part_number=ESP32S-HiLetgo]

nets:
  N1: R1.Pin_0, LED1.cathode
  N2: R1.Pin_1, IOE1.P0
  N3: LED1.anode, R2.Pin_0, LED2.anode, LED3.anode, LED4.anode, LED5.anode, LED6.anode, LED7.anode, LED8.anode, IOE1.Vcc, U1.3.3
  N4: R2.Pin_1, IOE1.INT'
  N5: R3.Pin_0, LED2.cathode
  N6: R3.Pin_1, IOE1.P1
  N7: R4.Pin_0, LED3.cathode
  N8: R4.Pin_1, IOE1.P2
  N9: R5.Pin_0, LED4.cathode
  N10: R5.Pin_1, IOE1.P3
  N11: R6.Pin_0, LED5.cathode
  N12: R6.Pin_1, IOE1.P4
  N13: LED6.cathode, R8.Pin_0
  N14: LED7.cathode, R9.Pin_0
  N15: LED8.cathode, R7.Pin_0
  N16: R7.Pin_1, IOE1.P5
  N17: R8.Pin_1, IOE1.P6
  N18: R9.Pin_1, IOE1.P7
  N19: IOE1.A0, IOE1.A1, IOE1.A2, IOE1.Ground, U1.GND
  N20: IOE1.SCL, U1.GPIO22
  N21: IOE1.SDA, U1.GPIO21

custom parts:
  Pca95x4: The PCA95x4 provides 8 bits of General Purpose parallel Input/Output (GPIO) expansion for I2C-bus applications.
  ESP32S-HiLetgo: HiLetgo ESP-WROOM-32 ESP32 ESP-32S Development Board 2.4GHz Dual-Mode WiFi + Bluetooth Dual Cores Microcontroller The ESP32 integrated with Antenna switches, RF Balun, power amplifiers, low-noise amplifiers, filters, and management modules, and the entire solution occupies the least area of PCB. 2.4 GHz Wi-Fi plus Bluetooth dual-mode chip, with TSMC Ultra-low power consumption 40nm technology,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
