# Fritzing sketch RotaryEncoder.Sample (saved by Fritzing 0.9.3b)

parts:
  RE1 = Switched Rotary Encoder [package=THT]
  U1 = ESP32S-HiLetgo [part_number=ESP32S-HiLetgo]

nets:
  N1: RE1.EncoderPinA, U1.GPIO21
  N2: RE1.EncoderPinC, U1.GND
  N3: RE1.EncoderPinB, U1.GPIO19

custom parts:
  Switched Rotary Encoder: Rotary Encoder from ALPS STEC12E07.
  ESP32S-HiLetgo: HiLetgo ESP-WROOM-32 ESP32 ESP-32S Development Board 2.4GHz Dual-Mode WiFi + Bluetooth Dual Cores Microcontroller The ESP32 integrated with Antenna switches, RF Balun, power amplifiers, low-noise amplifiers, filters, and management modules, and the entire solution occupies the least area of PCB. 2.4 GHz Wi-Fi plus Bluetooth dual-mode chip, with TSMC Ultra-low power consumption 40nm technology,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
