# Fritzing sketch rtc (saved by Fritzing 0.9.8b)

parts:
  U1 = ESP32-38PinWide [part_number=ESP32-38PinWide]
  Part1 = Real Time Clock Module - DS1307 RTC Breakout Board

nets:
  N1: U1.GPIO11, Part1.GND
  VIN: U1.VIN, Part1.5V
  N2: U1.GPIO21, Part1.SDA
  N3: U1.GPIO22, Part1.SCL

custom parts:
  ESP32-38PinWide: Generic 38-Pin ESP32 with wide format (only access to one side of pins on a breadboard) based on Stephen Lilley's HiLetgo ESP-WROOM-32 ESP32 ESP-32S Development Board.
