# Fritzing sketch Si7021_I2c_Read_Temp_Humidity (saved by Fritzing 0.9.3b)
breadboards: 1

parts:
  Part1 = Adafruit Si7021 Temp Humidity [part_number="Adafruit #3251"]
  U1 = ESP32S-HiLetgo [part_number=ESP32S-HiLetgo]

nets:
  N1: Part1.SDA, U1.GPIO21
  N2: Part1.SCL, U1.GPIO22
  GND: Part1.GND, U1.GND
  N3: Part1.VIN, U1.3.3

custom parts:
  Adafruit Si7021 Temp Humidity: It's summer and you're sweating and your hair's all frizzy and all you really want to know is why the weatherman said this morning that today's relative humidity would max out at a perfectly reasonable 42% when it feels more like 77%. Enter the Si7021 Temperature + Humidity Sensor - the best way to prove the weatherman wrong! This lovely sensor for Silicon labs has ± 3% relative humidity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
  ESP32S-HiLetgo: HiLetgo ESP-WROOM-32 ESP32 ESP-32S Development Board 2.4GHz Dual-Mode WiFi + Bluetooth Dual Cores Microcontroller The ESP32 integrated with Antenna switches, RF Balun, power amplifiers, low-noise amplifiers, filters, and management modules, and the entire solution occupies the least area of PCB. 2.4 GHz Wi-Fi plus Bluetooth dual-mode chip, with TSMC Ultra-low power consumption 40nm technology,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
