# Fritzing sketch sn74hc595-led-bar-graph-spi (saved by Fritzing 0.9.3b)
breadboards: 1

parts:
  U1 = 74HC595 [package="DIP16 [THT]"]
  D1 = LED_BARGRAPH_10 [package=led_bargaph_10]
  R1 = Resistor [tolerance=±5% resistance=220 package="1206 [SMD]"]
  R2 = Resistor [tolerance=±5% resistance=220 package="1206 [SMD]"]
  R4 = Resistor [tolerance=±5% resistance=220 package="1206 [SMD]"]
  R7 = Resistor [tolerance=±5% resistance=220 package="1206 [SMD]"]
  R9 = Resistor [tolerance=±5% resistance=220 package="1206 [SMD]"]
  R10 = Resistor [tolerance=±5% resistance=220 package="1206 [SMD]"]
  R11 = Resistor [tolerance=±5% resistance=220 package="1206 [SMD]"]
  R12 = Resistor [tolerance=±5% resistance=220 package="1206 [SMD]"]
  U2 = ESP32S-HiLetgo [part_number=ESP32S-HiLetgo]

nets:
  N1: U1.Q1, D1.B_A
  N2: U1.Q2, D1.C_A
  N3: U1.Q3, D1.D_A
  N4: U1.Q4, D1.E_A
  N5: U1.Q5, D1.F_A
  N6: U1.Q6, D1.G_A
  N7: U1.Q7, D1.H_A
  GND: U1.GND, U1.OE, R1.Pin_0, R2.Pin_0, R4.Pin_0, R7.Pin_0, R9.Pin_0, R10.Pin_0, R11.Pin_0, R12.Pin_0, U2.GND
  VCC: U1.MR, U1.VCC, U2.VIN
  N8: U1.SH_CP, U2.GPIO5
  N9: U1.ST_CP, U2.GPIO18
  N10: U1.DS, U2.GPIO13
  N11: U1.Q0, D1.A_A
  N12: D1.J_C, D1.C_C, R12.Pin_1
  N13: D1.H_C, R10.Pin_1
  N14: D1.G_C, R11.Pin_1
  N15: D1.F_C, R9.Pin_1
  N16: D1.E_C, R7.Pin_1
  N17: D1.D_C, R1.Pin_1
  N18: D1.B_C, R4.Pin_1
  N19: D1.A_C, R2.Pin_1

custom parts:
  ESP32S-HiLetgo: HiLetgo ESP-WROOM-32 ESP32 ESP-32S Development Board 2.4GHz Dual-Mode WiFi + Bluetooth Dual Cores Microcontroller The ESP32 integrated with Antenna switches, RF Balun, power amplifiers, low-noise amplifiers, filters, and management modules, and the entire solution occupies the least area of PCB. 2.4 GHz Wi-Fi plus Bluetooth dual-mode chip, with TSMC Ultra-low power consumption 40nm technology,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
