# Fritzing sketch Ssd1306_I2c_PiOled (saved by Fritzing 0.9.3b)

parts:
  Part1 = Adafruit 128x32 Pi OLED [part_number="Adafruit #3527"]
  U1 = ESP32S-HiLetgo [part_number=ESP32S-HiLetgo]

nets:
  +5V: Part1.+5V, U1.VIN
  N1: Part1.SDA, U1.GPIO21
  N2: Part1.SCL, U1.GPIO22
  GND: Part1.GND, U1.GND

custom parts:
  Adafruit 128x32 Pi OLED: If you're looking for the most compact li'l display for a Raspberry Pi (most likely a Pi Zero) project, this might be just the thing you need! The Adafruit 128x32 PiOLED is your little OLED pal, ready to snap onto any and all Raspberry Pi computers, to give you a little display. The PiOLED comes with a monochrome 128x32 OLED, with sharp white pixels. The OLED uses only the I2C pins so you have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
  ESP32S-HiLetgo: HiLetgo ESP-WROOM-32 ESP32 ESP-32S Development Board 2.4GHz Dual-Mode WiFi + Bluetooth Dual Cores Microcontroller The ESP32 integrated with Antenna switches, RF Balun, power amplifiers, low-noise amplifiers, filters, and management modules, and the entire solution occupies the least area of PCB. 2.4 GHz Wi-Fi plus Bluetooth dual-mode chip, with TSMC Ultra-low power consumption 40nm technology,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
