# Fritzing sketch tsl256x (saved by Fritzing 0.9.9b)

parts:
  U1 = ESP32S-HiLetgo [part_number=ESP32S-HiLetgo]
  Part2 = Adafruit TSL2561 [part_number="Adafruit #439"]

nets:
  N1: U1.3.3, Part2.VIN
  N2: U1.GPIO4, Part2.INT
  N3: U1.GPIO21, Part2.SDA
  N4: U1.GPIO22, Part2.SCL
  GND: U1.GND, Part2.GND

custom parts:
  ESP32S-HiLetgo: HiLetgo ESP-WROOM-32 ESP32 ESP-32S Development Board 2.4GHz Dual-Mode WiFi + Bluetooth Dual Cores Microcontroller The ESP32 integrated with Antenna switches, RF Balun, power amplifiers, low-noise amplifiers, filters, and management modules, and the entire solution occupies the least area of PCB. 2.4 GHz Wi-Fi plus Bluetooth dual-mode chip, with TSMC Ultra-low power consumption 40nm technology,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
  Adafruit TSL2561: The TSL2561 luminosity sensor is an advanced digital light sensor, ideal for use in a wide range of light situations. Compared to low cost CdS cells, this sensor is more precise, allowing for exact lux calculations and can be configured for different gain/timing ranges to detect light ranges from up to 0.1 - 40,000+ Lux on the fly. The best part of this sensor is that it contains both infrared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
