# Fritzing sketch Uln2003 (saved by Fritzing 0.9.3b)

parts:
  MOTOR1 = 28BYJ-48 Stepper Motor
  VCC1 = Battery block 9V
  BREAKOUT1 = ULN2003A breakout board
  U1 = ESP32S-HiLetgo [part_number=ESP32S-HiLetgo]

nets:
  N1: MOTOR1.BLUE, BREAKOUT1.BLUE_wire
  N2: MOTOR1.PINK, BREAKOUT1.PINK_wire
  N3: MOTOR1.RED, BREAKOUT1.RED_wire
  N4: MOTOR1.ORANGE, BREAKOUT1.ORANGE_wire
  N5: MOTOR1.YELLOW, BREAKOUT1.YELLOW_wire
  N6: VCC1.-, BREAKOUT1.0V, U1.GND
  N7: VCC1.+, BREAKOUT1.+5V
  N8: BREAKOUT1.In_1, U1.GPIO10
  N9: BREAKOUT1.In_2, U1.GPIO13
  N10: BREAKOUT1.In_3, U1.GPIO12
  N11: BREAKOUT1.In_4, U1.GPIO14

custom parts:
  28BYJ-48 Stepper Motor: 28BYJ-48 gear-reduction stepper motor (small)
  ULN2003A breakout board: ULN2003A 7-way Darlington Transistor Driver on breakoutboard
  ESP32S-HiLetgo: HiLetgo ESP-WROOM-32 ESP32 ESP-32S Development Board 2.4GHz Dual-Mode WiFi + Bluetooth Dual Cores Microcontroller The ESP32 integrated with Antenna switches, RF Balun, power amplifiers, low-noise amplifiers, filters, and management modules, and the entire solution occupies the least area of PCB. 2.4 GHz Wi-Fi plus Bluetooth dual-mode chip, with TSMC Ultra-low power consumption 40nm technology,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
