# Fritzing sketch ws2812B (saved by Fritzing 0.9.9b)

parts:
  U1 = ESP32S-HiLetgo [part_number=ESP32S-HiLetgo]
  NEOPIXEL1 = Neopixel Strip -- White (60/m)

nets:
  N1: U1.VIN, NEOPIXEL1.DI
  N2: U1.GPIO23, NEOPIXEL1.+5V
  GND: U1.GND, NEOPIXEL1.GND

custom parts:
  ESP32S-HiLetgo: HiLetgo ESP-WROOM-32 ESP32 ESP-32S Development Board 2.4GHz Dual-Mode WiFi + Bluetooth Dual Cores Microcontroller The ESP32 integrated with Antenna switches, RF Balun, power amplifiers, low-noise amplifiers, filters, and management modules, and the entire solution occupies the least area of PCB. 2.4 GHz Wi-Fi plus Bluetooth dual-mode chip, with TSMC Ultra-low power consumption 40nm technology,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
  Neopixel Strip -- White (60/m): Neopixel Strip, White, 60 pixels per meter.
