# Fritzing sketch ESP32-ePaper-Sketch (saved by Fritzing 0.9.10b)

parts:
  U2 = ESP32-38PinWide [part_number=ESP32-38PinWide]
  Part1 = Adafruit 1.54" Tri-Color eInk / ePaper Display with SRAM [part_number=3625]

nets:
  N1: U2.3.3, Part1.3.3V
  N2: U2.GPIO15, Part1.RESET
  N3: U2.GPIO4, Part1.BUSY
  N4: U2.GPIO16, Part1.DISPCS
  N5: U2.GPIO18, Part1.SCLK
  N6: U2.GPIO3, Part1.DC
  N7: U2.GPIO23, Part1.MISO
  GND: U2.GND, Part1.GND

custom parts:
  ESP32-38PinWide: Generic 38-Pin ESP32 with wide format (only access to one side of pins on a breadboard) based on Stephen Lilley's HiLetgo ESP-WROOM-32 ESP32 ESP-32S Development Board.
  Adafruit 1.54" Tri-Color eInk / ePaper Display with SRAM: This small 1.54" tri-color display has 152x152 black and red ink pixels and a white-ish background. Using our Arduino library, you can create a 'frame buffer' with what pixels you want to have activated and then write that out to the display. We tossed a small SRAM chip on the back. This chip shares the SPI port the eInk display uses, so you only need one extra pin. And, no more frame-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
